# Fritzing sketch circuit (saved by Fritzing 0.9.3b)
breadboards: 1

parts:
  Part1 = Arduino Uno (Rev3)
  U1 = LCD-16X2 [package=lcd-16x2]
  R1 = Rotary Potentiometer (Large) [maximum_resistance=100kΩ package=THT]
  Part2 = Real Time Clock Module - DS1307 RTC Breakout Board
  S1 = Round Pushbutton

nets:
  N1: Part1.A4/SDA, Part2.SQW
  N2: Part1.A5/SCL, Part2.SCL
  N3: Part1.D8, S1.leg1
  N4: Part1.D11_PWM/MOSI, U1.E
  N5: Part1.D12/MISO, U1.RS
  GND: Part1.GND, U1.VSS, U1.R_W, U1.K, R1.leg1, Part2.GND
  N6: Part1.D2, U1.DB7
  N7: Part1.D3_PWM, U1.DB6
  N8: Part1.D4, U1.DB5
  N9: Part1.D5_PWM, U1.DB4
  5V: Part1.5V, U1.VDD, U1.A, R1.leg2, Part2.5V, S1.leg0
  N10: U1.VO, R1.wiper
